# Fritzing sketch FARESHARE PCB 2.1 (saved by Fritzing 0.9.10b)
circuit board: 6.88566cm x 5.36311cm

parts:
  Nema_17 = Stepper Motor - Bipolar
  Motor_Control_A4988 = Pololu A4988 [package=SO16]
  Barrel_Jack_(12V) = Power plug
  R1 = Resistor [tolerance=±5% power=0.25 resistance=1M package=THT]
  J1 = molex pin header, 5 pins [form=molex]
  Part3 = Arduino Ethernet Shield (Rev3)
  100uF = Capacitor Polarized [package=cpol-radial-1000uf-25v]
  S1 = Momentary Switch [package=ksa_sealed_tac_switch]

nets:
  N1: Nema_17.A, Motor_Control_A4988.2B
  N2: Nema_17.C, Motor_Control_A4988.2A
  N3: Nema_17.B, Motor_Control_A4988.1A
  N4: Nema_17.D, Motor_Control_A4988.1B
  N5: Motor_Control_A4988.RESET, Motor_Control_A4988.SLEEP
  N6: Motor_Control_A4988.STEP, Part3.PWM_D5
  N7: Motor_Control_A4988.DIR, Part3.SDCS
  GND: Motor_Control_A4988.GND, Barrel_Jack_(12V).GND, J1.pin3, Part3.GND, 100uF.-, S1.3
  VDD: Motor_Control_A4988.VDD, J1.pin2, Part3.3V3
  VCC: Motor_Control_A4988.VMOT, Barrel_Jack_(12V).VCC, Part3.VIN, 100uF.+
  N8: R1.Pin_0, Part3.PWM_D3
  N9: R1.Pin_1, J1.pin1, Part3.D2
  N10: J1.pin4, Part3.D7
  N11: J1.pin5, Part3.PWM_D11
  N12: Part3.D8, S1.1

notes:
  1000μF
  Barrel Jack
  D0
  Rst
  2B
  2A
  1A
  1B
  Khokhar Lab
  GND
  3V3
  FARE
  A4988
  Motor
  RFID
  1MΩ
  SHARE
  Lks
  Prime
